// Logisim project Arq.Computadores I.circ as structural Verilog: 2 circuits, main circuit main
module main (
  input  A,
  input  B,
  input  C,
  output vai_1,
  output S
);

  add_1 add_1_1 (.S(S), .vai_1(vai_1), .A(A), .B(C), .C(B));
endmodule

module add_1 (
  input  A,
  input  B,
  input  C,
  output S,
  output vai_1
);

  wire and_1_out, and_2_out, xor_1_out, xor_2_out;

  xor xor_1 (xor_1_out, C, B);
  xor xor_2 (xor_2_out, C, B);
  xor xor_3 (S, xor_1_out, A);
  and and_1 (and_1_out, xor_2_out, A);
  and and_2 (and_2_out, C, B);
  or or_1 (vai_1, and_1_out, and_2_out);
endmodule
