// Logisim project CPU_4bits (1).circ as structural Verilog: 16 circuits, main circuit main
module main (
  input  in_1,
  input  [3:0] in_2,
  input  in_3,
  output overflow,
  output zero
);

  wire clock_1_out, clock_2_out, clock_3_out, not_1_out, not_2_out;
  wire [3:0] ac_1_s, counter_1_q, overflow_s, ram_1_data, ula_1_s;
  wire [7:0] rom_1_data;

  not not_1 (not_1_out, in_1);
  Counter #(.width(4), .max('hf)) counter_1 (
    .load(in_1), .D(in_2), .count(not_1_out), .Q(counter_1_q), .clk(clock_1_out));  // open: carry, clr
  Clock clock_1 (.out(clock_1_out));
  uc uc_1 ();  // open: instrução, clock, reset, rst_pc, o, z, dados, operando, E, opcode, load, ir, pc, ac, ram, r_w
  ROM #(.addrWidth(4)) rom_1 (.addr(counter_1_q), .data(rom_1_data));  // open: sel
  Clock clock_2 (.out(clock_2_out));
  ULA ula_1 (
    .D(rom_1_data[4]), .B(overflow_s), .A(ac_1_s), .in_4(rom_1_data[7:5]), .zero(zero), .overflow(overflow),
    .S(ula_1_s));
  Mux u_overflow (.E(rom_1_data[3:0]), .C(rom_1_data[4]), .D(ram_1_data), .S(overflow_s));
  AC ac_1 (.clock(clock_2_out), .E(ula_1_s), .S(ac_1_s));
  RAM #(.addrWidth(4), .dataWidth(4)) ram_1 (
    .addr(rom_1_data[3:0]), .data(ram_1_data), .clk(clock_3_out), .ld(in_3));  // open: sel, clr
  Clock clock_3 (.out(clock_3_out));
  not not_2 (not_2_out, in_3);
  buffer buffer_1 (.E(ac_1_s), .in_2(not_2_out), .S(ram_1_data));
endmodule

module Sub_1 (
  input  A,
  input  B,
  input  C,
  output S,
  output Vai_1
);

  wire and_1_out, and_2_out, or_1_out, xor_1_out;

  xor xor_1 (xor_1_out, C, B);
  or or_1 (or_1_out, C, B);
  xor xor_2 (S, xor_1_out, A);
  and and_1 (and_1_out, or_1_out, ~A);  // AND_Gate
  and and_2 (and_2_out, C, B);
  or or_2 (Vai_1, and_1_out, and_2_out);
endmodule

module Sub_4 (
  input  [3:0] in_1,
  input  [3:0] in_2,
  output out_3,
  output [3:0] out_4
);

  wire sub_1_2_vai_1, sub_1_3_vai_1, sub_1_4_vai_1;

  Sub_1 sub_1_1 (.S(out_4[3]), .Vai_1(out_3), .A(in_1[3]), .B(in_2[3]), .C(sub_1_2_vai_1));
  Sub_1 sub_1_2 (.S(out_4[2]), .Vai_1(sub_1_2_vai_1), .A(in_1[2]), .B(in_2[2]), .C(sub_1_4_vai_1));
  Sub_1 sub_1_3 (.S(out_4[0]), .Vai_1(sub_1_3_vai_1), .A(in_1[0]), .B(in_2[0]), .C(1'b0));
  Sub_1 sub_1_4 (.S(out_4[1]), .Vai_1(sub_1_4_vai_1), .A(in_1[1]), .B(in_2[1]), .C(sub_1_3_vai_1));
endmodule

module add_1 (
  input  in_1,
  input  in_2,
  input  in_3,
  output out_4,
  output out_5
);

  wire and_1_out, and_2_out, xor_1_out, xor_2_out;

  xor xor_1 (xor_1_out, in_3, in_2);
  xor xor_2 (xor_2_out, in_3, in_2);
  xor xor_3 (out_4, xor_1_out, in_1);
  and and_1 (and_1_out, xor_2_out, in_1);
  and and_2 (and_2_out, in_3, in_2);
  or or_1 (out_5, and_1_out, and_2_out);
endmodule

module add_4 (
  input  [3:0] B,
  input  [3:0] A,
  output out_3,
  output [3:0] S
);

  wire add_1_2_out_5, add_1_3_out_5, add_1_4_out_5;

  add_1 add_1_1 (.out_4(S[3]), .out_5(out_3), .in_1(A[3]), .in_2(B[3]), .in_3(add_1_2_out_5));
  add_1 add_1_2 (.out_4(S[2]), .out_5(add_1_2_out_5), .in_1(A[2]), .in_2(B[2]), .in_3(add_1_3_out_5));
  add_1 add_1_3 (.out_4(S[1]), .out_5(add_1_3_out_5), .in_1(A[1]), .in_2(B[1]), .in_3(add_1_4_out_5));
  add_1 add_1_4 (.out_4(S[0]), .out_5(add_1_4_out_5), .in_1(A[0]), .in_2(B[0]), .in_3(1'b0));
endmodule

module rot_esq (
  input  [3:0] abcd,
  input  [1:0] xy,
  output [3:0] ABCD_2
);

  wire and_1_out, and_2_out, and_3_out, and_4_out, and_5_out, and_6_out, and_7_out, and_8_out, and_9_out;

  and and_1 (and_1_out, ~xy[1], ~xy[0], abcd[3]);  // AND_Gate
  and and_2 (and_2_out, ~xy[1], xy[0], abcd[2]);  // AND_Gate
  and and_3 (and_3_out, xy[1], ~xy[0], abcd[1]);  // AND_Gate
  and and_4 (and_4_out, xy[1], xy[0], abcd[0]);
  and and_5 (and_5_out, ~xy[1], ~xy[0], abcd[2]);  // AND_Gate
  and and_6 (and_6_out, ~xy[1], xy[0], abcd[1]);  // AND_Gate
  and and_7 (and_7_out, xy[1], ~xy[0]);  // AND_Gate
  and and_8 (and_8_out, ~xy[1], ~xy[0], abcd[1]);  // AND_Gate
  and and_9 (and_9_out, ~xy[1], xy[0], abcd[0]);  // AND_Gate
  and and_10 (ABCD_2[3], ~xy[1], ~xy[0], abcd[0]);  // AND_Gate
  or or_1 (ABCD_2[3], and_1_out, and_2_out, and_3_out, and_4_out);
  or or_2 (ABCD_2[3], and_5_out, and_6_out, and_7_out);
  or or_3 (ABCD_2[3], and_8_out, and_9_out);

  assign ABCD_2[2:0] = {3{ABCD_2[3]}};
endmodule

module ret_dir (
  input  [3:0] abcd,
  input  [1:0] xy,
  output [3:0] ABCD_2
);

  wire and_1_out, and_2_out, and_3_out, and_4_out, and_5_out, and_6_out, and_7_out, and_8_out, and_9_out;

  and and_1 (and_1_out, ~xy[1], ~xy[0], abcd[0]);  // AND_Gate
  and and_2 (and_2_out, ~xy[1], xy[0], abcd[1]);  // AND_Gate
  and and_3 (and_3_out, xy[1], ~xy[0], abcd[2]);  // AND_Gate
  and and_4 (and_4_out, xy[1], xy[0], abcd[3]);
  and and_5 (and_5_out, ~xy[1], ~xy[0], abcd[1]);  // AND_Gate
  and and_6 (and_6_out, ~xy[1], xy[0], abcd[2]);  // AND_Gate
  and and_7 (and_7_out, xy[1], ~xy[0]);  // AND_Gate
  and and_8 (and_8_out, ~xy[1], ~xy[0], abcd[2]);  // AND_Gate
  and and_9 (and_9_out, ~xy[1], xy[0], abcd[3]);  // AND_Gate
  and and_10 (ABCD_2[3], ~xy[1], ~xy[0], abcd[3]);  // AND_Gate
  or or_1 (ABCD_2[0], and_1_out, and_2_out, and_3_out, and_4_out);
  or or_2 (ABCD_2[1], and_5_out, and_6_out, and_7_out);
  or or_3 (ABCD_2[2], and_8_out, and_9_out);
endmodule

module dec_3x8 (
  input  [2:0] in_1,
  output s0,
  output s1,
  output s2,
  output s3,
  output s4,
  output s5,
  output s6,
  output s7
);

  wire not_1_out, not_2_out, not_3_out, not_4_out, not_5_out, not_6_out, not_7_out, not_8_out, not_9_out,
       not_10_out, not_11_out, not_12_out;

  not not_1 (not_1_out, in_1[2]);
  not not_2 (not_2_out, in_1[1]);
  not not_3 (not_3_out, in_1[0]);
  not not_4 (not_4_out, in_1[2]);
  not not_5 (not_5_out, in_1[1]);
  not not_6 (not_6_out, in_1[2]);
  not not_7 (not_7_out, in_1[0]);
  not not_8 (not_8_out, in_1[2]);
  not not_9 (not_9_out, in_1[1]);
  not not_10 (not_10_out, in_1[0]);
  not not_11 (not_11_out, in_1[1]);
  not not_12 (not_12_out, in_1[0]);
  and and_1 (s0, not_1_out, not_2_out, not_3_out);
  and and_2 (s1, not_4_out, not_5_out, in_1[0]);
  and and_3 (s2, not_6_out, in_1[1], not_7_out);
  and and_4 (s3, not_8_out, in_1[1], in_1[0]);
  and and_5 (s4, in_1[2], not_9_out, not_10_out);
  and and_6 (s5, in_1[2], not_11_out, in_1[0]);
  and and_7 (s6, in_1[2], in_1[1], not_12_out);
  and and_8 (s7, in_1[2], in_1[1], in_1[0]);
endmodule

module or_4 (
  input  [3:0] B,
  input  [3:0] A,
  output [3:0] S
);

  or or_1 (S[3], A[3], B[3]);
  or or_2 (S[2], A[2], B[2]);
  or or_3 (S[1], A[1], B[1]);
  or or_4 (S[0], A[0], B[0]);
endmodule

module not_4 (
  input  [3:0] E,
  output [3:0] S
);

  not not_1 (S[2], E[2]);
  not not_2 (S[3], E[3]);
  not not_3 (S[1], E[1]);
  not not_4 (S[0], E[0]);
endmodule

module buffer (
  input  [3:0] E,
  input  in_2,
  output [3:0] S
);

  assign S[3] = in_2 ? E[3] : 1'bz;  // Controlled_Buffer controlled_buffer_1
  assign S[2] = in_2 ? E[2] : 1'bz;  // Controlled_Buffer controlled_buffer_2
  assign S[1] = in_2 ? E[1] : 1'bz;  // Controlled_Buffer controlled_buffer_3
  assign S[0] = in_2 ? E[0] : 1'bz;  // Controlled_Buffer controlled_buffer_4
endmodule

module ULA (
  input  D,
  input  [3:0] B,
  input  [3:0] A,
  input  [2:0] in_4,
  output overflow,
  output [3:0] S,
  output zero
);

  wire add_4_1_out_3, and_1_out, and_2_out, dec_3x8_1_s0, dec_3x8_1_s1, dec_3x8_1_s2, dec_3x8_1_s3,
       dec_3x8_1_s4, dec_3x8_1_s5, dec_3x8_1_s6, dec_3x8_1_s7, not_1_out, sub_4_1_out_3;
  wire [3:0] add_4_1_s, buffer_7_s, not_4_1_s, or_4_1_s, ret_dir_1_abcd_2, rot_esq_1_abcd_2, sub_4_1_out_4;

  or or_1 (overflow, and_1_out, and_2_out);
  and and_1 (and_1_out, add_4_1_out_3, dec_3x8_1_s1);
  and and_2 (and_2_out, sub_4_1_out_3, dec_3x8_1_s2);
  buffer buffer_1 (.E(B), .in_2(dec_3x8_1_s0), .S(S));
  dec_3x8 dec_3x8_1 (
    .s0(dec_3x8_1_s0), .s1(dec_3x8_1_s1), .s2(dec_3x8_1_s2), .s3(dec_3x8_1_s3), .s4(dec_3x8_1_s4),
    .s5(dec_3x8_1_s5), .s6(dec_3x8_1_s6), .s7(dec_3x8_1_s7), .in_1(in_4));
  Sub_4 sub_4_1 (.in_1(A), .in_2(B), .out_4(sub_4_1_out_4), .out_3(sub_4_1_out_3));
  add_4 add_4_1 (.B(B), .A(A), .S(add_4_1_s), .out_3(add_4_1_out_3));
  buffer buffer_2 (.E(add_4_1_s), .in_2(dec_3x8_1_s1), .S(S));
  buffer buffer_3 (.E(sub_4_1_out_4), .in_2(dec_3x8_1_s2), .S(S));
  or_4 or_4_1 (.A(A), .S(or_4_1_s), .B(B));
  buffer buffer_4 (.E(or_4_1_s), .in_2(dec_3x8_1_s3), .S(S));
  nor nor_1 (zero, S[0], S[1], S[2], S[3], dec_3x8_1_s6, dec_3x8_1_s7);
  not_4 not_4_1 (.E(B), .S(not_4_1_s));
  buffer buffer_5 (.E(not_4_1_s), .in_2(dec_3x8_1_s4), .S(S));
  not not_1 (not_1_out, D);
  rot_esq rot_esq_1 (.abcd(A), .xy(B[1:0]), .ABCD_2(rot_esq_1_abcd_2));
  ret_dir ret_dir_1 (.ABCD_2(ret_dir_1_abcd_2), .abcd(A), .xy(B[1:0]));
  buffer buffer_6 (.E(buffer_7_s), .in_2(dec_3x8_1_s5), .S(S));
  buffer buffer_7 (.E(rot_esq_1_abcd_2), .in_2(not_1_out), .S(buffer_7_s));
  buffer buffer_8 (.E(ret_dir_1_abcd_2), .in_2(D), .S(buffer_7_s));
endmodule

module AC (
  input  clock,
  input  [3:0] E,
  output [3:0] S
);

  D_Flip_Flop d_ff_1 (.clk(clock), .D(E[3]), .Q(S[3]));  // open: Qn, preset, en, reset
  D_Flip_Flop d_ff_2 (.clk(clock), .D(E[2]), .Q(S[2]));  // open: Qn, preset, en, reset
  D_Flip_Flop d_ff_3 (.clk(clock), .D(E[1]), .Q(S[1]));  // open: Qn, preset, en, reset
  D_Flip_Flop d_ff_4 (.clk(clock), .D(E[0]), .Q(S[0]));  // open: Qn, preset, en, reset
endmodule

module Mux (
  input  [3:0] E,
  input  [3:0] D,
  input  C,
  output [3:0] S
);

  wire not_1_out;

  buffer buffer_1 (.E(E), .in_2(not_1_out), .S(S));
  not not_1 (not_1_out, C);
  buffer buffer_2 (.E(D), .in_2(C), .S(S));
endmodule

module ir (
  input  clock,
  input  [7:0] E,
  output [7:0] S
);

  D_Flip_Flop D7 (.clk(clock), .D(E[7]), .Q(S[7]));  // open: Qn, preset, en, reset
  D_Flip_Flop D6 (.clk(clock), .D(E[6]), .Q(S[6]));  // open: Qn, preset, en, reset
  D_Flip_Flop D5 (.clk(clock), .D(E[5]), .Q(S[5]));  // open: Qn, preset, en, reset
  D_Flip_Flop D4 (.clk(clock), .D(E[4]), .Q(S[4]));  // open: Qn, preset, en, reset
  D_Flip_Flop D3 (.clk(clock), .D(E[3]), .Q(S[3]));  // open: Qn, preset, en, reset
  D_Flip_Flop D2 (.clk(clock), .D(E[2]), .Q(S[2]));  // open: Qn, preset, en, reset
  D_Flip_Flop D1 (.clk(clock), .D(E[1]), .Q(S[1]));  // open: Qn, preset, en, reset
  D_Flip_Flop D0 (.clk(clock), .D(E[0]), .Q(S[0]));  // open: Qn, preset, en, reset
endmodule

// r/w
module uc (
  input  z,
  input  [7:0] \instrução ,
  input  clock,
  input  reset,
  input  o,
  output ir,
  output pc,
  output ac,
  output ram,
  output [3:0] dados,
  output rst_pc,
  output [3:0] operando,
  output E,
  output [2:0] opcode,
  output r_w,
  output load
);

  wire goto_out, jpo_out, jpz_out;
  wire [1:0] counter_1_q;

  Counter #(.width(2), .max('h3)) counter_1 (.Q(counter_1_q), .clk(clock), .clr(reset));  // open: load, D, count, carry
  nand stor (r_w, ac, \instrução [7], \instrução [6], \instrução [5], \instrução [4]);
  and and_1 (ir, ~counter_1_q[1], ~counter_1_q[0]);  // AND_Gate
  and jpo (jpo_out, \instrução [7], \instrução [6], ~\instrução [5], \instrução [4], pc, o);  // AND_Gate
  and and_2 (ac, counter_1_q[1], ~counter_1_q[0]);  // AND_Gate
  and and_3 (ram, counter_1_q[1], counter_1_q[0]);
  and and_4 (pc, ~counter_1_q[1], counter_1_q[0]);  // AND_Gate
  and jpz (jpz_out, \instrução [7], \instrução [6], ~\instrução [5], ~\instrução [4], pc, z);  // AND_Gate
  and goto (goto_out, \instrução [7], \instrução [6], \instrução [5], ~\instrução [4], pc);  // AND_Gate
  or or_1 (load, goto_out, jpz_out, jpo_out);

  assign dados = \instrução [3:0];
  assign E = \instrução [4];
  assign opcode = \instrução [7:5];
  assign operando = \instrução [3:0];
  assign rst_pc = reset;
endmodule
