// Logisim project CPU_4bits.circ as structural Verilog
module Sub_1 (
  input  A,
  input  B,
  input  C,
  output S,
  output Vai_1
);

  wire and_1_out, and_2_out, or_1_out, xor_1_out;

  xor xor_1 (xor_1_out, C, B);
  or or_1 (or_1_out, C, B);
  xor xor_2 (S, xor_1_out, A);
  and and_1 (and_1_out, or_1_out, ~A);  // AND_Gate
  and and_2 (and_2_out, C, B);
  or or_2 (Vai_1, and_1_out, and_2_out);
endmodule

module Sub_4 (
  input  [3:0] in_1,
  input  [3:0] in_2,
  output out_3,
  output [3:0] out_4
);

  wire sub_1_2_vai_1, sub_1_3_vai_1, sub_1_4_vai_1;

  Sub_1 sub_1_1 (.S(out_4[3]), .Vai_1(out_3), .A(in_1[3]), .B(in_2[3]), .C(sub_1_2_vai_1));
  Sub_1 sub_1_2 (.S(out_4[2]), .Vai_1(sub_1_2_vai_1), .A(in_1[2]), .B(in_2[2]), .C(sub_1_4_vai_1));
  Sub_1 sub_1_3 (.S(out_4[0]), .Vai_1(sub_1_3_vai_1), .A(in_1[0]), .B(in_2[0]), .C(1'b0));
  Sub_1 sub_1_4 (.S(out_4[1]), .Vai_1(sub_1_4_vai_1), .A(in_1[1]), .B(in_2[1]), .C(sub_1_3_vai_1));
endmodule

module add_1 (
  input  in_1,
  input  in_2,
  input  in_3,
  output out_4,
  output out_5
);

  wire and_1_out, and_2_out, xor_1_out, xor_2_out;

  xor xor_1 (xor_1_out, in_3, in_2);
  xor xor_2 (xor_2_out, in_3, in_2);
  xor xor_3 (out_4, xor_1_out, in_1);
  and and_1 (and_1_out, xor_2_out, in_1);
  and and_2 (and_2_out, in_3, in_2);
  or or_1 (out_5, and_1_out, and_2_out);
endmodule

module add_4 (
  input  [3:0] B,
  input  [3:0] A,
  output out_3,
  output [3:0] S
);

  wire add_1_2_out_5, add_1_3_out_5, add_1_4_out_5;

  add_1 add_1_1 (.out_4(S[3]), .out_5(out_3), .in_1(A[3]), .in_2(B[3]), .in_3(add_1_2_out_5));
  add_1 add_1_2 (.out_4(S[2]), .out_5(add_1_2_out_5), .in_1(A[2]), .in_2(B[2]), .in_3(add_1_3_out_5));
  add_1 add_1_3 (.out_4(S[1]), .out_5(add_1_3_out_5), .in_1(A[1]), .in_2(B[1]), .in_3(add_1_4_out_5));
  add_1 add_1_4 (.out_4(S[0]), .out_5(add_1_4_out_5), .in_1(A[0]), .in_2(B[0]), .in_3(1'b0));
endmodule

module rot_esq (
  input  [3:0] abcd,
  input  [1:0] xy,
  output [3:0] ABCD_2
);

  wire and_1_out, and_2_out, and_3_out, and_4_out, and_5_out, and_6_out, and_7_out, and_8_out, and_9_out;

  and and_1 (and_1_out, ~xy[1], ~xy[0], abcd[3]);  // AND_Gate
  and and_2 (and_2_out, ~xy[1], xy[0], abcd[2]);  // AND_Gate
  and and_3 (and_3_out, xy[1], ~xy[0], abcd[1]);  // AND_Gate
  and and_4 (and_4_out, xy[1], xy[0], abcd[0]);
  and and_5 (and_5_out, ~xy[1], ~xy[0], abcd[2]);  // AND_Gate
  and and_6 (and_6_out, ~xy[1], xy[0], abcd[1]);  // AND_Gate
  and and_7 (and_7_out, xy[1], ~xy[0]);  // AND_Gate
  and and_8 (and_8_out, ~xy[1], ~xy[0], abcd[1]);  // AND_Gate
  and and_9 (and_9_out, ~xy[1], xy[0], abcd[0]);  // AND_Gate
  and and_10 (ABCD_2[3], ~xy[1], ~xy[0], abcd[0]);  // AND_Gate
  or or_1 (ABCD_2[3], and_1_out, and_2_out, and_3_out, and_4_out);
  or or_2 (ABCD_2[3], and_5_out, and_6_out, and_7_out);
  or or_3 (ABCD_2[3], and_8_out, and_9_out);

  assign ABCD_2[2:0] = {3{ABCD_2[3]}};
endmodule

module ret_dir (
  input  [3:0] abcd,
  input  [1:0] xy,
  output [3:0] ABCD_2
);

  wire and_1_out, and_2_out, and_3_out, and_4_out, and_5_out, and_6_out, and_7_out, and_8_out, and_9_out;

  and and_1 (and_1_out, ~xy[1], ~xy[0], abcd[0]);  // AND_Gate
  and and_2 (and_2_out, ~xy[1], xy[0], abcd[1]);  // AND_Gate
  and and_3 (and_3_out, xy[1], ~xy[0], abcd[2]);  // AND_Gate
  and and_4 (and_4_out, xy[1], xy[0], abcd[3]);
  and and_5 (and_5_out, ~xy[1], ~xy[0], abcd[1]);  // AND_Gate
  and and_6 (and_6_out, ~xy[1], xy[0], abcd[2]);  // AND_Gate
  and and_7 (and_7_out, xy[1], ~xy[0]);  // AND_Gate
  and and_8 (and_8_out, ~xy[1], ~xy[0], abcd[2]);  // AND_Gate
  and and_9 (and_9_out, ~xy[1], xy[0], abcd[3]);  // AND_Gate
  and and_10 (ABCD_2[3], ~xy[1], ~xy[0], abcd[3]);  // AND_Gate
  or or_1 (ABCD_2[0], and_1_out, and_2_out, and_3_out, and_4_out);
  or or_2 (ABCD_2[1], and_5_out, and_6_out, and_7_out);
  or or_3 (ABCD_2[2], and_8_out, and_9_out);
endmodule

module dec_3x8 (
  input  [2:0] in_1,
  output s0,
  output s1,
  output s2,
  output s3,
  output s4,
  output s5,
  output s6,
  output s7
);

  wire not_1_out, not_2_out, not_3_out, not_4_out, not_5_out, not_6_out, not_7_out, not_8_out, not_9_out,
       not_10_out, not_11_out, not_12_out;

  not not_1 (not_1_out, in_1[2]);
  not not_2 (not_2_out, in_1[1]);
  not not_3 (not_3_out, in_1[0]);
  not not_4 (not_4_out, in_1[2]);
  not not_5 (not_5_out, in_1[1]);
  not not_6 (not_6_out, in_1[2]);
  not not_7 (not_7_out, in_1[0]);
  not not_8 (not_8_out, in_1[2]);
  not not_9 (not_9_out, in_1[1]);
  not not_10 (not_10_out, in_1[0]);
  not not_11 (not_11_out, in_1[1]);
  not not_12 (not_12_out, in_1[0]);
  and and_1 (s0, not_1_out, not_2_out, not_3_out);
  and and_2 (s1, not_4_out, not_5_out, in_1[0]);
  and and_3 (s2, not_6_out, in_1[1], not_7_out);
  and and_4 (s3, not_8_out, in_1[1], in_1[0]);
  and and_5 (s4, in_1[2], not_9_out, not_10_out);
  and and_6 (s5, in_1[2], not_11_out, in_1[0]);
  and and_7 (s6, in_1[2], in_1[1], not_12_out);
  and and_8 (s7, in_1[2], in_1[1], in_1[0]);
endmodule
